// Logisim project exercise4.circ as structural Verilog: 1 circuit, main circuit main
module main (
);

  wire clock_1_out, d_ff_1_q, d_ff_2_q, nand_1_out, nand_2_out, nand_3_out, nand_4_out, nand_5_out,
       nand_6_out, nand_7_out, nand_8_out, nand_9_out, nand_10_out, nand_11_out, nand_12_out, nand_13_out,
       not_1_out, not_2_out, not_3_out, not_4_out, not_5_out, not_6_out, not_7_out, not_8_out, not_9_out;

  not not_1 (not_1_out, 1'b1);
  Clock clock_1 (.out(clock_1_out));
  not not_2 (not_2_out, 1'b1);
  not not_3 (not_3_out, d_ff_1_q);
  not not_4 (not_4_out, not_1_out);
  nand nand_1 (nand_1_out, not_3_out, 1'b1, not_4_out);
  nand nand_2 (nand_2_out, not_2_out, d_ff_2_q, d_ff_2_q);
  nand nand_3 (nand_3_out, 1'b1, not_1_out, d_ff_1_q);
  nand nand_4 (nand_4_out, nand_1_out, nand_2_out);
  not not_5 (not_5_out, nand_4_out);
  not not_6 (not_6_out, d_ff_2_q);
  nand nand_5 (nand_5_out, not_5_out, nand_3_out);
  nand nand_6 (nand_6_out, d_ff_1_q, not_2_out);
  nand nand_7 (nand_7_out, d_ff_2_q, not_4_out, 1'b1);
  nand nand_8 (nand_8_out, not_6_out, not_1_out, 1'b1);
  nand nand_9 (nand_9_out, nand_6_out, nand_7_out);
  not not_7 (not_7_out, nand_9_out);
  nand nand_10 (nand_10_out, not_7_out, nand_8_out);
  D_Flip_Flop d_ff_1 (.clk(clock_1_out), .D(nand_10_out), .Q(d_ff_1_q));  // open: Qn, preset, en, reset
  not not_8 (not_8_out, d_ff_2_q);
  not not_9 (not_9_out, d_ff_1_q);
  D_Flip_Flop d_ff_2 (.clk(clock_1_out), .D(nand_5_out), .Q(d_ff_2_q));  // open: Qn, preset, en, reset
  nand nand_11 (nand_11_out, not_8_out, d_ff_1_q);
  nand nand_12 (nand_12_out, not_9_out, d_ff_2_q);
  LED led_1 (.in(d_ff_2_q));
  LED led_2 (.in(nand_13_out));
  nand nand_13 (nand_13_out, nand_11_out, nand_12_out);

  // Notes on the sheet:
  //   x0
  //   x1
  //   D0
  //   D1
endmodule
